// Logisim project atividade4.circ as structural Verilog: 1 circuit, main circuit main
module main (
  input  A,
  input  B,
  input  C,
  input  D,
  output Y
);

  wire and_2_out, and_3_out, and_4_out, and_5_out, and_6_out, not_1_out, not_3_out, or_2_out, or_3_out;

  // AND_Gate and_1 is placed but not wired
  not not_1 (not_1_out, C);
  // OR_Gate or_1 is placed but not wired
  and and_2 (and_2_out, A, not_1_out);
  or or_2 (or_2_out, C, A);
  and and_3 (and_3_out, not_1_out, D);
  // NOT_Gate not_2 is placed but not wired
  and and_4 (and_4_out, and_2_out, B);
  not not_3 (not_3_out, and_3_out);
  and and_5 (and_5_out, or_2_out, and_2_out);
  or or_3 (or_3_out, and_4_out, not_3_out);
  and and_6 (and_6_out, or_3_out, and_5_out);
  not not_4 (Y, and_6_out);
endmodule
