// Logisim project aulaMemoria-arquivoMoodle.circ as structural Verilog: 11 circuits, main circuit main
module main (
);


  // Notes on the sheet:
  //   CIRCUITOS DE MEMÓRIA
endmodule

module clock (
  input  in_1,
  output out_2
);

  Clock clock_1 (.out(out_2));
endmodule

module latch_SR (
  input  S,
  input  R,
  output Q_prime,
  output Q
);

  nor nor_1 (Q_prime, S, Q);
  nor nor_2 (Q, Q_prime, R);
endmodule

module latch_SR_com_clock (
  input  S,
  input  CLOCK,
  input  R,
  output Q_prime,
  output Q
);

  wire and_1_out, and_2_out;

  and and_1 (and_1_out, S, CLOCK);
  and and_2 (and_2_out, CLOCK, R);
  nor nor_1 (Q_prime, and_1_out, Q);
  nor nor_2 (Q, Q_prime, and_2_out);
endmodule

module latch_D_com_clock (
  input  D,
  input  CLOCK,
  output Q_prime,
  output Q
);

  wire and_1_out, and_2_out, not_1_out;

  not not_1 (not_1_out, D);
  and and_1 (and_1_out, D, CLOCK);
  and and_2 (and_2_out, CLOCK, not_1_out);
  nor nor_1 (Q_prime, and_1_out, Q);
  nor nor_2 (Q, Q_prime, and_2_out);
endmodule

module flipflop_D (
  input  D,
  input  CLOCK,
  input  D_2,
  input  CLOCK_2,
  input  D_3,
  input  D_4,
  output Q_prime,
  output Q,
  output Q_prime_2,
  output Q_2,
  output out_11,
  output out_12
);

  wire and_1_out, and_2_out, and_3_out, and_4_out, and_5_out, and_6_out, clock_1_out, clock_2_out, not_1_out,
       not_2_out, not_3_out, not_4_out;

  not not_1 (not_1_out, CLOCK);
  Clock clock_1 (.out(clock_1_out));
  and and_1 (and_1_out, not_1_out, CLOCK);
  not not_2 (not_2_out, D);
  not not_3 (not_3_out, D_2);
  not not_4 (not_4_out, CLOCK_2);
  and and_2 (and_2_out, not_4_out, CLOCK_2);
  Clock u_clock_2 (.out(clock_2_out));
  and and_3 (and_3_out, D, and_1_out);
  and and_4 (and_4_out, and_1_out, not_2_out);
  and and_5 (and_5_out, D_2, clock_1_out);
  and and_6 (and_6_out, clock_1_out, not_3_out);
  D_Flip_Flop d_ff_1 (.clk(and_2_out), .D(D_3), .Q(out_11));  // open: Qn, preset, en, reset
  D_Flip_Flop d_ff_2 (.clk(clock_2_out), .D(D_4), .Q(out_12));  // open: Qn, preset, en, reset
  nor nor_1 (Q_prime, and_3_out, Q);
  nor nor_2 (Q, Q_prime, and_4_out);
  nor nor_3 (Q_prime_2, and_5_out, Q_2);
  nor nor_4 (Q_2, Q_prime_2, and_6_out);

  // Notes on the sheet:
  //   Q_prime: pull=up
  //   Q_prime_2: pull=up
endmodule

module registrador (
  input  [3:0] D,
  input  CLOCK,
  input  ENABLE,
  input  RESET,
  output [3:0] out_5
);

  D_Flip_Flop d_ff_1 (.clk(CLOCK), .D(D[3]), .Q(out_5[3]), .en(ENABLE), .reset(RESET));  // open: Qn, preset
  D_Flip_Flop d_ff_2 (.clk(CLOCK), .D(D[2]), .Q(out_5[2]), .en(ENABLE), .reset(RESET));  // open: Qn, preset
  D_Flip_Flop d_ff_3 (.clk(CLOCK), .D(D[1]), .Q(out_5[1]), .en(ENABLE), .reset(RESET));  // open: Qn, preset
  D_Flip_Flop d_ff_4 (.clk(CLOCK), .D(D[0]), .Q(out_5[0]), .en(ENABLE), .reset(RESET));  // open: Qn, preset
endmodule

module somador_1bit (
  input  vem_um,
  input  A,
  input  B,
  output soma,
  output vai_um
);

  wire and_1_out, and_2_out, and_3_out, and_4_out, and_5_out, and_6_out, and_7_out, and_8_out, not_1_out,
       not_2_out, not_3_out, not_4_out, not_5_out, not_6_out, not_7_out, not_8_out, not_9_out;

  not not_1 (not_1_out, vem_um);
  not not_2 (not_2_out, vem_um);
  not not_3 (not_3_out, vem_um);
  not not_4 (not_4_out, A);
  not not_5 (not_5_out, A);
  not not_6 (not_6_out, A);
  not not_7 (not_7_out, B);
  not not_8 (not_8_out, B);
  not not_9 (not_9_out, B);
  and and_1 (and_1_out, not_1_out, not_4_out, B);
  and and_2 (and_2_out, not_2_out, A, not_7_out);
  and and_3 (and_3_out, vem_um, not_5_out, not_8_out);
  and and_4 (and_4_out, vem_um, A, B);
  and and_5 (and_5_out, not_3_out, A, B);
  and and_6 (and_6_out, vem_um, not_6_out, B);
  and and_7 (and_7_out, vem_um, A, not_9_out);
  and and_8 (and_8_out, vem_um, A, B);
  or or_1 (soma, and_1_out, and_2_out, and_3_out, and_4_out);
  or or_2 (vai_um, and_5_out, and_6_out, and_7_out, and_8_out);
endmodule

module somador (
  input  in_1,
  input  in_2,
  input  in_3,
  input  in_4,
  input  in_5,
  input  in_6,
  output S3,
  output S2,
  output S1,
  output S0
);

  wire bit0_vai_um, bit1_vai_um;

  somador_1bit bit0 (.vem_um(1'b0), .A(in_6), .B(in_3), .soma(S0), .vai_um(bit0_vai_um));
  somador_1bit bit1 (.vem_um(bit0_vai_um), .A(in_5), .B(in_2), .soma(S1), .vai_um(bit1_vai_um));
  somador_1bit bit2 (.vem_um(bit1_vai_um), .A(in_4), .B(in_1), .soma(S2), .vai_um(S3));

  // Notes on the sheet:
  //   110
  //   0000011
  //   00000011
  //   ___+___________
  //   00000110
endmodule

module somador_com_registrador (
  input  in_1,
  input  in_2,
  input  in_3,
  input  in_4,
  input  in_5,
  input  in_6,
  input  CLOCK,
  output S3,
  output S2,
  output S1,
  output S0
);

  wire bit0_vai_um, bit1_vai_um;
  wire [3:0] bit0_soma;

  somador_1bit bit0 (.vem_um(1'b0), .A(in_6), .B(in_3), .soma(bit0_soma[0]), .vai_um(bit0_vai_um));
  somador_1bit bit1 (.vem_um(bit0_vai_um), .A(in_5), .B(in_2), .soma(bit0_soma[1]), .vai_um(bit1_vai_um));
  somador_1bit bit2 (.vem_um(bit1_vai_um), .A(in_4), .B(in_1), .soma(bit0_soma[2]), .vai_um(bit0_soma[3]));
  registrador registrador (.D(bit0_soma), .CLOCK(CLOCK), .ENABLE(1'b1), .RESET(1'b0), .out_5({S3, S2, S1, S0}));
endmodule

module memoria_4x4 (
  input  [3:0] ENTRADA,
  input  [1:0] \ENDEREÇO ,
  input  CS,
  input  RD,
  input  OE,
  output [3:0] \SAÍDA 
);

  wire and_1_out, and_2_out, and_3_out, and_4_out, and_5_out, and_6_out, and_7_out, and_8_out, and_9_out,
       and_10_out, and_11_out, and_12_out, and_13_out, and_14_out, and_15_out, and_16_out, and_17_out,
       and_18_out, and_19_out, and_20_out, and_21_out, and_22_out, and_23_out, and_24_out, and_25_out,
       and_26_out, d_ff_1_q, d_ff_2_q, d_ff_3_q, d_ff_4_q, d_ff_5_q, d_ff_6_q, d_ff_7_q, d_ff_8_q, d_ff_9_q,
       d_ff_10_q, d_ff_11_q, d_ff_12_q, d_ff_13_q, d_ff_14_q, d_ff_15_q, d_ff_16_q, not_1_out, not_2_out,
       not_3_out, not_4_out, not_5_out;
  wire [3:0] or_4_out;

  not not_1 (not_1_out, \ENDEREÇO [0]);
  not not_2 (not_2_out, \ENDEREÇO [1]);
  not not_3 (not_3_out, \ENDEREÇO [1]);
  not not_4 (not_4_out, \ENDEREÇO [0]);
  and and_1 (and_1_out, not_1_out, not_2_out);
  and and_2 (and_2_out, \ENDEREÇO [0], not_3_out);
  and and_3 (and_3_out, not_4_out, \ENDEREÇO [1]);
  and and_4 (and_4_out, \ENDEREÇO [0], \ENDEREÇO [1]);
  and and_5 (and_5_out, CS, not_5_out);
  not not_5 (not_5_out, RD);
  and and_6 (and_6_out, and_1_out, and_5_out);
  and and_7 (and_7_out, and_2_out, and_5_out);
  and and_8 (and_8_out, and_3_out, and_5_out);
  and and_9 (and_9_out, and_4_out, and_5_out);
  and and_10 (and_10_out, CS, RD, OE);
  D_Flip_Flop d_ff_1 (.clk(and_6_out), .D(ENTRADA[3]), .Q(d_ff_1_q));  // open: Qn, preset, en, reset
  and and_11 (and_11_out, and_1_out, d_ff_1_q);
  D_Flip_Flop d_ff_2 (.clk(and_7_out), .D(ENTRADA[3]), .Q(d_ff_2_q));  // open: Qn, preset, en, reset
  and and_12 (and_12_out, and_2_out, d_ff_2_q);
  D_Flip_Flop d_ff_3 (.clk(and_8_out), .D(ENTRADA[3]), .Q(d_ff_3_q));  // open: Qn, preset, en, reset
  and and_13 (and_13_out, and_3_out, d_ff_3_q);
  D_Flip_Flop d_ff_4 (.clk(and_9_out), .D(ENTRADA[3]), .Q(d_ff_4_q));  // open: Qn, preset, en, reset
  and and_14 (and_14_out, and_4_out, d_ff_4_q);
  or or_1 (or_4_out[3], and_14_out, and_13_out, and_12_out, and_11_out);
  D_Flip_Flop d_ff_5 (.clk(and_6_out), .D(ENTRADA[2]), .Q(d_ff_5_q));  // open: Qn, preset, en, reset
  D_Flip_Flop d_ff_6 (.clk(and_7_out), .D(ENTRADA[2]), .Q(d_ff_6_q));  // open: Qn, preset, en, reset
  D_Flip_Flop d_ff_7 (.clk(and_8_out), .D(ENTRADA[2]), .Q(d_ff_7_q));  // open: Qn, preset, en, reset
  D_Flip_Flop d_ff_8 (.clk(and_9_out), .D(ENTRADA[2]), .Q(d_ff_8_q));  // open: Qn, preset, en, reset
  and and_15 (and_15_out, and_1_out, d_ff_5_q);
  and and_16 (and_16_out, and_2_out, d_ff_6_q);
  and and_17 (and_17_out, and_3_out, d_ff_7_q);
  and and_18 (and_18_out, and_4_out, d_ff_8_q);
  or or_2 (or_4_out[2], and_18_out, and_17_out, and_16_out, and_15_out);
  D_Flip_Flop d_ff_9 (.clk(and_6_out), .D(ENTRADA[1]), .Q(d_ff_9_q));  // open: Qn, preset, en, reset
  and and_19 (and_19_out, and_1_out, d_ff_9_q);
  D_Flip_Flop d_ff_10 (.clk(and_7_out), .D(ENTRADA[1]), .Q(d_ff_10_q));  // open: Qn, preset, en, reset
  and and_20 (and_20_out, and_2_out, d_ff_10_q);
  D_Flip_Flop d_ff_11 (.clk(and_8_out), .D(ENTRADA[1]), .Q(d_ff_11_q));  // open: Qn, preset, en, reset
  and and_21 (and_21_out, and_3_out, d_ff_11_q);
  D_Flip_Flop d_ff_12 (.clk(and_9_out), .D(ENTRADA[1]), .Q(d_ff_12_q));  // open: Qn, preset, en, reset
  and and_22 (and_22_out, and_4_out, d_ff_12_q);
  or or_3 (or_4_out[1], and_22_out, and_21_out, and_20_out, and_19_out);
  D_Flip_Flop d_ff_13 (.clk(and_6_out), .D(ENTRADA[0]), .Q(d_ff_13_q));  // open: Qn, preset, en, reset
  and and_23 (and_23_out, and_1_out, d_ff_13_q);
  D_Flip_Flop d_ff_14 (.clk(and_7_out), .D(ENTRADA[0]), .Q(d_ff_14_q));  // open: Qn, preset, en, reset
  and and_24 (and_24_out, and_2_out, d_ff_14_q);
  D_Flip_Flop d_ff_15 (.clk(and_8_out), .D(ENTRADA[0]), .Q(d_ff_15_q));  // open: Qn, preset, en, reset
  and and_25 (and_25_out, and_3_out, d_ff_15_q);
  D_Flip_Flop d_ff_16 (.clk(and_9_out), .D(ENTRADA[0]), .Q(d_ff_16_q));  // open: Qn, preset, en, reset
  and and_26 (and_26_out, and_4_out, d_ff_16_q);
  or or_4 (or_4_out[0], and_26_out, and_25_out, and_24_out, and_23_out);
  assign \SAÍDA  = and_10_out ? or_4_out : 4'bz;  // Controlled_Buffer controlled_buffer_1

  // Notes on the sheet:
  //   ATIVIDADE: FAZER UMA MEMÓRIA 4X8
  //   MEMÓRIA 4X4
endmodule
